// Logisim project obligg1.circ as structural Verilog: 8 circuits, main circuit main
module main (
  input  [3:0] A,
  input  in_2
);

  wire [8:0] Multiplier_out_2, Negator_output;

  Multiplier Multiplier (.in_1(A), .out_2(Multiplier_out_2));
  Negator Negator (.Input(Multiplier_out_2), .Inverting_Signal(in_2), .Output(Negator_output));
  // Probe on Negator_output
  LED led_1 (.in(Negator_output[7]));
  LED led_2 (.in(Negator_output[6]));
  LED led_3 (.in(Negator_output[5]));
  LED MSB (.in(Negator_output[8]));
  LED led_4 (.in(Negator_output[3]));
  LED led_5 (.in(Negator_output[1]));
  LED led_6 (.in(Negator_output[2]));
  LED led_7 (.in(Negator_output[4]));
  LED LSB (.in(Negator_output[0]));
endmodule

module _8_bit_Adder (
  input  [7:0] B,
  input  [7:0] A,
  output [8:0] Sum
);

  wire fadder_1_carry_out, fadder_2_carry_out, fadder_3_carry_out, fadder_4_carry_out, fadder_5_carry_out,
       fadder_6_carry_out, hadder_1_carry_out;

  Hadder hadder_1 (.A(B[0]), .B(A[0]), .Sum(Sum[0]), .Carry_out(hadder_1_carry_out));
  Fadder fadder_1 (.A(A[3]), .B(B[3]), .Carry_In(fadder_2_carry_out), .Sum(Sum[3]), .Carry_Out(fadder_1_carry_out));
  Fadder fadder_2 (.A(A[2]), .B(B[2]), .Carry_In(fadder_3_carry_out), .Sum(Sum[2]), .Carry_Out(fadder_2_carry_out));
  Fadder fadder_3 (.A(A[1]), .B(B[1]), .Carry_In(hadder_1_carry_out), .Sum(Sum[1]), .Carry_Out(fadder_3_carry_out));
  Fadder fadder_4 (.A(A[5]), .B(B[5]), .Carry_In(fadder_5_carry_out), .Sum(Sum[5]), .Carry_Out(fadder_4_carry_out));
  Fadder fadder_5 (.A(A[4]), .B(B[4]), .Carry_In(fadder_1_carry_out), .Sum(Sum[4]), .Carry_Out(fadder_5_carry_out));
  Fadder fadder_6 (.A(A[6]), .B(B[6]), .Carry_In(fadder_4_carry_out), .Sum(Sum[6]), .Carry_Out(fadder_6_carry_out));
  Fadder fadder_7 (.A(A[7]), .B(B[7]), .Carry_In(fadder_6_carry_out), .Sum(Sum[7]), .Carry_Out(Sum[8]));

  // Notes on the sheet:
  //   Legger sammen 2 8-bit tall
endmodule

module _8 (
  input  [3:0] A,
  output [7:0] Output
);


  assign Output = {1'b0, A, 3'b000};

  // Notes on the sheet:
  //   Shifter A 3 til venstre
endmodule

module _2 (
  input  [3:0] A,
  output [7:0] Output
);


  assign Output = {3'b000, A, 1'b0};

  // Notes on the sheet:
  //   Shifter A 1 til venstre
endmodule

module Multiplier (
  input  [3:0] in_1,
  output [8:0] out_2
);

  wire [7:0] A_2_output, A_8_output;

  _2 A_2 (.A(in_1), .Output(A_2_output));
  _8 A_8 (.A(in_1), .Output(A_8_output));
  _8_bit_Adder A_2___a_8 (.A(A_2_output), .B(A_8_output), .Sum(out_2));

  // Notes on the sheet:
  //   Plusser sammen A*2 og A*8 med en 8-bit adder
endmodule

module Fadder (
  input  A,
  input  B,
  input  Carry_In,
  output Sum,
  output Carry_Out
);

  wire and_1_out, and_2_out, xor_1_out;

  and and_1 (and_1_out, A, B);
  xor xor_1 (xor_1_out, A, B);
  xor xor_2 (Sum, xor_1_out, Carry_In);
  and and_2 (and_2_out, xor_1_out, Carry_In);
  or or_1 (Carry_Out, and_2_out, and_1_out);

  // Notes on the sheet:
  //   Full adder
endmodule

module Hadder (
  input  A,
  input  B,
  output Sum,
  output Carry_out
);

  xor xor_1 (Sum, A, B);
  and and_1 (Carry_out, B, A);

  // Notes on the sheet:
  //   Half Adder
endmodule

module Negator (
  input  [8:0] Input,
  input  Inverting_Signal,
  output [8:0] Output
);

  wire hadder_1_carry_out, hadder_2_carry_out, hadder_3_carry_out, hadder_4_carry_out, hadder_5_carry_out,
       hadder_6_carry_out, hadder_7_carry_out, hadder_8_carry_out, xor_1_out, xor_2_out, xor_3_out,
       xor_4_out, xor_5_out, xor_6_out, xor_7_out, xor_8_out, xor_9_out;

  Hadder hadder_1 (.A(xor_9_out), .B(Inverting_Signal), .Sum(Output[0]), .Carry_out(hadder_1_carry_out));
  xor xor_1 (xor_1_out, Input[8], Inverting_Signal);
  xor xor_2 (xor_2_out, Input[7], Inverting_Signal);
  xor xor_3 (xor_3_out, Input[6], Inverting_Signal);
  xor xor_4 (xor_4_out, Input[5], Inverting_Signal);
  xor xor_5 (xor_5_out, Input[4], Inverting_Signal);
  xor xor_6 (xor_6_out, Input[3], Inverting_Signal);
  xor xor_7 (xor_7_out, Input[2], Inverting_Signal);
  xor xor_8 (xor_8_out, Input[1], Inverting_Signal);
  xor xor_9 (xor_9_out, Input[0], Inverting_Signal);
  Hadder hadder_2 (.A(xor_8_out), .B(hadder_1_carry_out), .Sum(Output[1]), .Carry_out(hadder_2_carry_out));
  Hadder hadder_3 (.A(xor_7_out), .B(hadder_2_carry_out), .Sum(Output[2]), .Carry_out(hadder_3_carry_out));
  Hadder hadder_4 (.A(xor_6_out), .B(hadder_3_carry_out), .Sum(Output[3]), .Carry_out(hadder_4_carry_out));
  Hadder hadder_5 (.A(xor_5_out), .B(hadder_4_carry_out), .Sum(Output[4]), .Carry_out(hadder_5_carry_out));
  Hadder hadder_6 (.A(xor_3_out), .B(hadder_7_carry_out), .Sum(Output[6]), .Carry_out(hadder_6_carry_out));
  Hadder hadder_7 (.A(xor_4_out), .B(hadder_5_carry_out), .Sum(Output[5]), .Carry_out(hadder_7_carry_out));
  Hadder hadder_8 (.A(xor_2_out), .B(hadder_6_carry_out), .Sum(Output[7]), .Carry_out(hadder_8_carry_out));
  xor xor_10 (Output[8], hadder_8_carry_out, xor_1_out);

  // Notes on the sheet:
  //   Hvis inverting signal er på, så ganger den Input med -1 ved å switche alle bitsene og deretter legge til 1
endmodule
