// Logisim project obligg2.circ as structural Verilog: 6 circuits, main circuit main
module main (
);

  wire and_1_out, and_2_out, Clock_out, Inst_reader_load_lsb, Inst_reader_load_msb, Inst_reader_load_r,
       Inst_reader_no_op, Inst_reader_write_r, not_1_out, not_2_out, not_3_out, or_1_out, or_2_out, rst_out;
  wire [3:0] controlled_buffer_1_out, Inst_reader_data, teller_med_1_register_1_out;
  wire [7:0] controlled_buffer_2_out, r_selector_1_new_r, Register___R_q, rom_1_data;

  Clock Clock (.out(Clock_out));
  Button rst (.out(rst_out));
  // Probe on teller_med_1_register_1_out
  teller_med_1_register teller_med_1_register_1 (.In(not_1_out), .Reset(rst_out), .Out(teller_med_1_register_1_out));
  not not_1 (not_1_out, Clock_out);
  ROM #(.addrWidth(4)) rom_1 (.addr(teller_med_1_register_1_out), .data(rom_1_data));  // open: sel
  instruction_reader Inst_reader (
    .Instructions(rom_1_data), .load_lsb(Inst_reader_load_lsb), .Load_msb(Inst_reader_load_msb),
    .Load_R(Inst_reader_load_r), .data(Inst_reader_data), .Write_R(Inst_reader_write_r),
    .No_OP(Inst_reader_no_op));
  not not_2 (not_2_out, Inst_reader_no_op);
  assign controlled_buffer_1_out = not_2_out ? Inst_reader_data : 4'bz;  // Controlled_Buffer controlled_buffer_1
  // Probe on Inst_reader_data
  or or_1 (or_1_out, Inst_reader_load_msb, Inst_reader_load_r, Inst_reader_load_lsb);
  r_selector r_selector_1 (
    .DATA(controlled_buffer_1_out), .Old_R(controlled_buffer_2_out), .Change_LSB(Inst_reader_load_lsb),
    .Change_MSB(Inst_reader_load_msb), .new_R(r_selector_1_new_r));
  or or_2 (or_2_out, Inst_reader_load_r, Inst_reader_no_op);
  Register #(.trigger("falling")) Register___R (
    .D(r_selector_1_new_r), .en(or_1_out), .Q(Register___R_q), .clk(Clock_out), .clr(rst_out));
  not not_3 (not_3_out, or_2_out);
  assign controlled_buffer_2_out = not_3_out ? Register___R_q : 8'bz;  // Controlled_Buffer controlled_buffer_2
  and and_1 (and_1_out, Inst_reader_write_r, Clock_out);
  RAM #(.addrWidth(4)) ram_1 (
    .addr(controlled_buffer_1_out), .data(controlled_buffer_2_out), .clk(and_1_out), .ld(and_2_out),
    .clr(rst_out));  // open: sel
  and and_2 (and_2_out, Inst_reader_load_r, Clock_out);

  // Notes on the sheet:
  //   Instruction Block
  //   contents of rom_1 (hex, n*v repeats v):
  //   85 97 b1 81 94 a1
  //   Resets the counter, register and ram segment
  //   R selector
  //   Adress/Data
  //   The instruction bus ->
  //   Memory
endmodule

module Hadder (
  input  A,
  input  B,
  output Sum,
  output Carry_out
);

  xor xor_1 (Sum, A, B);
  and and_1 (Carry_out, B, A);

  // Notes on the sheet:
  //   Half Adder
endmodule

module teller_med_1_register (
  input  In,
  input  Reset,
  output [3:0] Out
);

  wire [3:0] adder_1_out;

  Adder #(.width(4)) adder_1 (.a(Out), .b(4'b0001), .out(adder_1_out));  // open: cin, cout
  Register #(.width(4)) register_1 (.D(adder_1_out), .en(1'b1), .Q(Out), .clk(In), .clr(Reset));
  // Probe on Out
endmodule

module instruction_reader (
  input  [7:0] Instructions,
  output load_lsb,
  output Load_msb,
  output Load_R,
  output Write_R,
  output No_OP,
  output [3:0] data
);

  wire not_1_out, not_2_out, not_3_out, not_4_out;
  wire [3:0] bitselector_1_out;

  BitSelector #(.group(4)) bitselector_1 (.in(Instructions), .out(bitselector_1_out), .sel(1'b1));
  BitSelector #(.group(4)) bitselector_2 (.in(Instructions), .out(data), .sel(1'b0));
  Comparator #(.width(4)) comparator_1 (.a(4'b1000), .b(bitselector_1_out), .eq(load_lsb));  // open: gt, lt
  Comparator #(.width(4)) comparator_2 (.a(4'b1001), .b(bitselector_1_out), .eq(Load_msb));  // open: gt, lt
  Comparator #(.width(4)) comparator_3 (.a(4'b1010), .b(bitselector_1_out), .eq(Load_R));  // open: gt, lt
  Comparator #(.width(4)) comparator_4 (.a(4'b1011), .b(bitselector_1_out), .eq(Write_R));  // open: gt, lt
  not not_1 (not_1_out, Write_R);
  not not_2 (not_2_out, Load_R);
  and and_1 (No_OP, not_1_out, not_2_out, not_3_out, not_4_out, 1'b1);
  not not_3 (not_3_out, Load_msb);
  not not_4 (not_4_out, load_lsb);
endmodule

module r_selector (
  input  [3:0] DATA,
  input  [7:0] Old_R,
  input  Change_LSB,
  input  Change_MSB,
  output [7:0] new_R
);

  wire [3:0] bitselector_1_out, bitselector_2_out;

  BitSelector #(.group(4)) bitselector_1 (.in(Old_R), .out(bitselector_1_out), .sel(1'b0));
  BitSelector #(.group(4)) bitselector_2 (.in(Old_R), .out(bitselector_2_out), .sel(1'b1));
  Multiplexer #(.width(4)) multiplexer_1 (
    .in0(bitselector_1_out), .in1(DATA), .out(new_R[3:0]), .sel(Change_LSB));  // open: en
  Multiplexer #(.width(4)) multiplexer_2 (
    .in0(bitselector_2_out), .in1(DATA), .out(new_R[7:4]), .sel(Change_MSB));  // open: en
endmodule

module main_with_open_bus (
);

  wire and_1_out, and_2_out, Clock_out, Inst_reader_load_lsb, Inst_reader_load_msb, Inst_reader_load_r,
       Inst_reader_no_op, not_1_out, not_2_out, or_1_out, rst_out;
  wire [3:0] Inst_reader_data, teller_med_1_register_1_out;
  wire [7:0] controlled_buffer_1_out, R_q, R_Selector_new_r, rom_1_data;

  Clock Clock (.out(Clock_out));
  Button rst (.out(rst_out));
  // Probe on teller_med_1_register_1_out
  teller_med_1_register teller_med_1_register_1 (.In(not_1_out), .Reset(rst_out), .Out(teller_med_1_register_1_out));
  not not_1 (not_1_out, Clock_out);
  ROM #(.addrWidth(4)) rom_1 (.addr(teller_med_1_register_1_out), .data(rom_1_data));  // open: sel
  // Probe on Inst_reader_data
  instruction_reader Inst_reader (
    .Instructions(rom_1_data), .load_lsb(Inst_reader_load_lsb), .Load_msb(Inst_reader_load_msb),
    .Load_R(Inst_reader_load_r), .data(Inst_reader_data), .No_OP(Inst_reader_no_op));  // open: Write_R
  or or_1 (or_1_out, Inst_reader_load_msb, Inst_reader_load_r, Inst_reader_load_lsb);
  r_selector R_Selector (
    .DATA(Inst_reader_data), .Old_R(controlled_buffer_1_out), .Change_LSB(Inst_reader_load_lsb),
    .Change_MSB(Inst_reader_load_msb), .new_R(R_Selector_new_r));
  Register #(.trigger("falling")) R (.D(R_Selector_new_r), .en(or_1_out), .Q(R_q), .clk(not_1_out), .clr(rst_out));
  not not_2 (not_2_out, Inst_reader_load_r);
  assign controlled_buffer_1_out = not_2_out ? R_q : 8'bz;  // Controlled_Buffer controlled_buffer_1
  and and_1 (and_1_out, Inst_reader_no_op, not_1_out);
  RAM #(.addrWidth(4)) ram_1 (
    .addr(Inst_reader_data), .data(controlled_buffer_1_out), .clk(and_1_out), .ld(and_2_out), .clr(rst_out));  // open: sel
  and and_2 (and_2_out, Inst_reader_load_r, not_1_out);

  // Notes on the sheet:
  //   Instructons
  //   contents of rom_1 (hex, n*v repeats v):
  //   8c 9d b0 b3 81 91 a0 b4
  //   Memory
endmodule
